# Fritzing sketch sketch (saved by Fritzing 0.9.3b)

parts:
  Part2 = Arduino Uno (Rev3)
  RS485_module3 = RS485 Module (MAX3485)
  RS485_module4 = RS485 Module (MAX3485)
  M2 = Pzem-004t
  U2 = RELAY [package=relay-jzc]
  Part4 = Arduino Mega 2560 (Rev3)
  RS485_module7 = RS485 Module (MAX3485)
  RS485_module8 = RS485 Module (MAX3485)
  RS485_module9 = RS485 Module (MAX3485)
  RS485_module10 = RS485 Module (MAX3485)
  Part5 = Arduino Uno (Rev3)
  RS485_module11 = RS485 Module (MAX3485)
  RS485_module12 = RS485 Module (MAX3485)
  M3 = Pzem-004t
  U3 = RELAY [package=relay-jzc]
  Part6 = Arduino Uno (Rev3)
  RS485_module13 = RS485 Module (MAX3485)
  RS485_module14 = RS485 Module (MAX3485)
  M4 = Pzem-004t
  U4 = RELAY [package=relay-jzc]
  Part7 = Dragino LoRa Shield V1.4
  Part8 = Arduino Uno (Rev3)  # not connected
  Part9 = Dragino LoRa Shield V1.4
  Gizwits_WiFi_Witty_ESP-12F1 = Gizwits WiFi Witty ESP-12F

nets:
  N1: Part2.D11_PWM/MOSI, M2.TX
  N2: Part2.D12/MISO, M2.RX
  N3: Part2.D0/RX, RS485_module3.RO
  N4: Part2.D1/TX, RS485_module4.DI
  N5: Part2.D5_PWM, U2.NC
  5V: Part2.5V, M2.5V
  GND: Part2.GND, RS485_module3.RE, RS485_module3.DE, M2.GND
  GND_2: RS485_module3.GND, RS485_module4.GND
  VCC: RS485_module3.VCC, RS485_module4.VCC
  N6: RS485_module4.A, RS485_module9.A
  N7: RS485_module4.B, RS485_module9.B
  N8: Part4.D19/RX1, RS485_module10.RO
  N9: Part4.D17_PWM/RX2, RS485_module9.RO
  N10: RS485_module7.A, RS485_module11.A
  N11: RS485_module7.B, RS485_module11.B
  N12: RS485_module7.RE, RS485_module7.DE
  N13: RS485_module7.DI, Part7.1
  GND_3: RS485_module8.A, RS485_module13.GND, RS485_module14.GND, RS485_module14.A
  N14: RS485_module8.B, RS485_module14.B
  N15: RS485_module8.RO, Part7.0
  N16: RS485_module8.DE, Part7.GND#44
  N17: RS485_module9.GND, Part7.GND#23
  VCC_2: RS485_module9.VCC, Part7.5V
  N18: RS485_module10.A, RS485_module12.A
  N19: RS485_module10.B, RS485_module12.B
  N20: Part5.D11_PWM/MOSI, M3.TX
  N21: Part5.D12/MISO, M3.RX
  N22: Part5.D0/RX, RS485_module11.RO
  N23: Part5.D1/TX, RS485_module12.DE, RS485_module12.DI
  N24: Part5.D5_PWM, U3.NC
  5V_2: Part5.5V, M3.5V
  GND_4: Part5.GND, RS485_module11.RE, RS485_module11.DE, M3.GND
  GND_5: RS485_module11.GND, RS485_module12.GND
  VCC_3: RS485_module11.VCC, RS485_module12.VCC
  N25: Part6.D11_PWM/MOSI, M4.TX
  N26: Part6.D12/MISO, M4.RX
  N27: Part6.D0/RX, RS485_module13.RO
  N28: Part6.D1/TX, RS485_module14.DI
  N29: Part6.D5_PWM, U4.NC
  5V_3: Part6.5V, M4.5V
  GND_6: Part6.GND, RS485_module13.RE, RS485_module13.DE, M4.GND
  VCC_4: RS485_module13.VCC, RS485_module14.VCC
  N30: Part9.1, Gizwits_WiFi_Witty_ESP-12F1.RXD
  N31: Part9.0, Gizwits_WiFi_Witty_ESP-12F1.TXD

custom parts:
  RS485 Module (MAX3485): Commercially available RS485 to RS232 TTL Module
  Pzem-004t: Pzem-004t used for measuring AC voltage, current, active power, frequency, power factor and active energy, the module is without display function, the data is read through the TTL interface.
